# Fritzing sketch 连线图 (saved by Fritzing 0.9.5d)
breadboards: 1

parts:
  U1 = ESP32-38PinWide [part_number=ESP32-38PinWide]
  元件1 = sensor_biometrico
  Grove1 = Grove OLED 128x96

nets:
  VCC: U1.3.3, 元件1.VCC, Grove1.VCC
  GND: U1.GPIO11, 元件1.GND, Grove1.GND
  N1: U1.GPIO16, 元件1.TX
  N2: U1.GPIO17, 元件1.RX
  N3: U1.GPIO21, Grove1.SDA
  N4: U1.GPIO22, Grove1.SCL

custom parts:
  ESP32-38PinWide: Generic 38-Pin ESP32 with wide format (only access to one side of pins on a breadboard) based on Stephen Lilley's HiLetgo ESP-WROOM-32 ESP32 ESP-32S Development Board.
  sensor_biometrico: Adafruit Optical Fingerprint Sensor
